# Fritzing sketch circuit_test (saved by Fritzing 0.9.6b)
breadboards: 1

parts:
  Part1 = Arduino Nano (Rev3.0)
  Mod1 = Raspberry Pi 4B
  Part3 = I2C level shifter bidirectional

nets:
  N1: Part1.D2, Part3.HV4
  N2: Part1.D4, Part3.HV3
  N3: Mod1.3V3, Part3.LV
  N4: Mod1.5V, Part3.HV
  N5: Mod1.ID_SC, Part3.GND
  N6: Mod1.GPIO20, Part3.LV3
  N7: Mod1.GPIO21, Part3.LV4
